// Logisim project muon3.circ as structural Verilog
module main (
);

  wire alu_1_carry_out, alu_1_eq, and_1_out, and_2_out, clock_1_out, dipswitch_1_sw3, dipswitch_1_sw5,
       io_subsystem_1_io_data_access, keybd_1_interrupt, keyboard_1_avail, microsequencer_1_a_write,
       microsequencer_1_a_write_indirect, microsequencer_1_alu_instruction,
       microsequencer_1_alu_instruction_logical, microsequencer_1_b_write, microsequencer_1_b_write_indirect,
       microsequencer_1_interrupt_enable, microsequencer_1_interrupt_safe, microsequencer_1_load,
       microsequencer_1_load_check, microsequencer_1_out_14, microsequencer_1_out_18,
       microsequencer_1_page_write, microsequencer_1_pc_enable, microsequencer_1_psw_compare, not_1_out,
       not_2_out, not_3_out, not_4_out, not_5_out, or_1_out, or_2_out, or_3_out, or_4_out, psw_1_branch,
       psw_1_interrupt, software_interrupt_1_interrupt, terminal_1_clock_out, undriven;
  wire [3:0] microsequencer_1_out_19, microsequencer_1_out_21;
  wire [5:0] io_subsystem_1_interrupt_handshake_return, io_subsystem_1_interupt_out,
       software_interrupt_1_interrupt_vector;
  wire [6:0] keyboard_1_data, terminal_1_out_5;
  wire [23:0] controlled_buffer_1_out, controlled_buffer_2_out, controlled_buffer_3_out,
       controlled_buffer_5_out, page_handler_1_out_5, pc_1_data_out, ram_1_dout;
  wire [23:4] microsequencer_1_out_19_2;

  DipSwitch dipswitch_1 (.sw3(dipswitch_1_sw3), .sw5(dipswitch_1_sw5));  // open: sw1, sw2, sw4, sw6, sw7, sw8
  Clock clock_1 (.out(clock_1_out));
  not not_1 (not_1_out, io_subsystem_1_io_data_access);
  software_interrupt software_interrupt_1 (
    .handshake(io_subsystem_1_interrupt_handshake_return), .clock(clock_1_out),
    .st_interrupt(microsequencer_1_out_18), .interrupt(software_interrupt_1_interrupt),
    .interrupt_vector(software_interrupt_1_interrupt_vector));
  and and_1 (and_1_out, or_3_out, not_1_out);
  timer timer_1 (
    .interrupt_handshake(io_subsystem_1_interrupt_handshake_return), .clock(clock_1_out),
    .out_4(software_interrupt_1_interrupt_vector));  // open: interrupt
  RAM #(.addrWidth(24), .dataWidth(24), .enables("line"), .\type ("nonvolatile")) ram_1 (
    .addr(page_handler_1_out_5), .we(and_1_out), .clk(clock_1_out), .din(controlled_buffer_1_out),
    .dout(ram_1_dout));
  assign controlled_buffer_1_out = not_2_out ? ram_1_dout : 24'bz;  // Controlled_Buffer controlled_buffer_1
  not not_2 (not_2_out, or_1_out);
  or or_1 (or_1_out, or_3_out, io_subsystem_1_io_data_access);
  IO_subsystem io_subsystem_1 (
    .data_in_IO(controlled_buffer_1_out), .Address_in_IO(controlled_buffer_5_out),
    .Interupt_1(software_interrupt_1_interrupt), .Interrupt_2(dipswitch_1_sw3), .interrupt_3(undriven),
    .interrrupt_4(keybd_1_interrupt), .interrupt_5(dipswitch_1_sw5),
    .interrupt_safety(microsequencer_1_interrupt_safe),
    .interrput_vector(software_interrupt_1_interrupt_vector), .interupt_out(io_subsystem_1_interupt_out),
    .interrupt_handshake_return(io_subsystem_1_interrupt_handshake_return),
    .IO_data_access(io_subsystem_1_io_data_access));  // open: Data_out_IO, Address_out_IO
  microsequencer microsequencer_1 (
    .clock(clock_1_out), .in_2(controlled_buffer_1_out), .branch(psw_1_branch), .WCS_write(and_2_out),
    .PC_enable(microsequencer_1_pc_enable), .load(microsequencer_1_load), .a_write(microsequencer_1_a_write),
    .B_write(microsequencer_1_b_write), .Page_write(microsequencer_1_page_write),
    .A_write_indirect(microsequencer_1_a_write_indirect),
    .B_write_indirect(microsequencer_1_b_write_indirect), .PSW_compare(microsequencer_1_psw_compare),
    .out_14(microsequencer_1_out_14), .ALU_instruction(microsequencer_1_alu_instruction),
    .ALU_instruction_logical(microsequencer_1_alu_instruction_logical),
    .Interrupt_enable(microsequencer_1_interrupt_enable), .out_18(microsequencer_1_out_18),
    .out_19({microsequencer_1_out_19_2, microsequencer_1_out_19}),
    .Interrupt_safe(microsequencer_1_interrupt_safe), .out_21(microsequencer_1_out_21),
    .load_check(microsequencer_1_load_check));  // open: load_another
  and and_2 (and_2_out, controlled_buffer_5_out[11], controlled_buffer_5_out[12], controlled_buffer_5_out[13], controlled_buffer_5_out[14], controlled_buffer_5_out[15], controlled_buffer_5_out[16], controlled_buffer_5_out[17], controlled_buffer_5_out[18], controlled_buffer_5_out[19], io_subsystem_1_io_data_access);
  or or_2 (or_2_out, microsequencer_1_a_write_indirect, microsequencer_1_b_write_indirect);
  or or_3 (or_3_out, microsequencer_1_alu_instruction, microsequencer_1_alu_instruction_logical);
  assign controlled_buffer_2_out = microsequencer_1_psw_compare ? {microsequencer_1_out_19_2, microsequencer_1_out_19} : 24'bz;  // Controlled_Buffer controlled_buffer_2
  // Digital_Oscilloscope digital_oscilloscope_1: pin names not known; wires that end beside it: clock_1_out, io_subsystem_1_io_data_access
  not not_3 (not_3_out, or_2_out);
  assign controlled_buffer_3_out = or_2_out ? controlled_buffer_1_out : 24'bz;  // Controlled_Buffer controlled_buffer_3
  assign controlled_buffer_3_out = not_3_out ? {microsequencer_1_out_19_2, microsequencer_1_out_19} : 24'bz;  // Controlled_Buffer controlled_buffer_4
  page_handler page_handler_1 (
    .in_1(controlled_buffer_5_out), .Page_in(microsequencer_1_out_19),
    .page_write(microsequencer_1_page_write), .clock(clock_1_out), .out_5(page_handler_1_out_5));
  PSW psw_1 (
    .compare_word_in(controlled_buffer_2_out), .clock(clock_1_out), .carry(alu_1_carry_out),
    .equals(alu_1_eq), .interrupt_lines(io_subsystem_1_interupt_out), .ALU_inst(or_3_out),
    .interrupt_enable_set(microsequencer_1_interrupt_enable), .Branch(psw_1_branch),
    .interrupt(psw_1_interrupt));  // open: interrupt_enable
  TERMINAL terminal_1 (
    .IO_data(controlled_buffer_1_out), .clock(clock_1_out), .IO_address(controlled_buffer_5_out[19:0]),
    .IO_write(io_subsystem_1_io_data_access), .out_5(terminal_1_out_5), .clock_out(terminal_1_clock_out));
  Keyboard keyboard_1 (
    .clk(clock_1_out), .re(not_4_out), .avail(keyboard_1_avail), .data(keyboard_1_data));  // open: clr
  not not_4 (not_4_out, keybd_1_interrupt);
  ALU alu_1 (
    .C_out(or_3_out), .A_write(microsequencer_1_a_write), .B_write(microsequencer_1_b_write),
    .clock(clock_1_out), .in_5(controlled_buffer_3_out), .ALU_inst(microsequencer_1_out_21),
    .ALU_logical(microsequencer_1_alu_instruction_logical), .out_8(controlled_buffer_1_out),
    .carry_out(alu_1_carry_out), .EQ(alu_1_eq));
  or or_4 (or_4_out, or_3_out, or_2_out);
  PC pc_1 (
    .load(microsequencer_1_load), .enable(microsequencer_1_pc_enable), .clock(clock_1_out),
    .data_in({microsequencer_1_out_19_2, microsequencer_1_out_19}), .interrupt(psw_1_interrupt),
    .PC_writeback(microsequencer_1_out_14), .Load_check(microsequencer_1_load_check), .data_out(pc_1_data_out));
  assign controlled_buffer_5_out = or_4_out ? {microsequencer_1_out_19_2, microsequencer_1_out_19} : 24'bz;  // Controlled_Buffer controlled_buffer_5
  not not_5 (not_5_out, or_4_out);
  assign controlled_buffer_5_out = not_5_out ? pc_1_data_out : 24'bz;  // Controlled_Buffer controlled_buffer_6
  TTY #(.cols(80), .rows(30)) tty_1 (.data(terminal_1_out_5), .clk(terminal_1_clock_out));  // open: we, clr
  keybd keybd_1 (
    .in_1(keyboard_1_avail), .in_2({1'b0, keyboard_1_data}), .clock(clock_1_out),
    .interrupt_handshake(io_subsystem_1_interrupt_handshake_return),
    .address_In(controlled_buffer_5_out[19:0]), .IO_write(io_subsystem_1_io_data_access),
    .data_out(controlled_buffer_1_out), .interrupt(keybd_1_interrupt),
    .out_9(software_interrupt_1_interrupt_vector));  // open: out_10
endmodule

module microsequencer (
  input  clock,
  input  [23:0] in_2,
  input  branch,
  input  WCS_write,
  output PC_enable,
  output load,
  output a_write,
  output B_write,
  output Page_write,
  output load_another,
  output A_write_indirect,
  output B_write_indirect,
  output PSW_compare,
  output out_14,
  output ALU_instruction,
  output ALU_instruction_logical,
  output Interrupt_enable,
  output out_18,
  output [23:0] out_19,
  output Interrupt_safe,
  output [3:0] out_21,
  output load_check
);

  wire and_3_out, branch_true_q, not_1_out, not_2_out, or_1_out, or_4_out;
  wire [3:0] counter_1_q;
  wire [7:0] and_1_out, and_2_out, controlled_buffer_1_out, ram_1_dout, register_1_q, rom_1_data;
  wire [7:7] j_k_ff_1_q;
  wire [9:0] decoder_1_out1;

  not not_1 (not_1_out, load_check);
  J_K_Flip_Flop #(.trigger("falling")) j_k_ff_1 (
    .J(not_1_out), .K(load_check), .clk(clock), .Q(j_k_ff_1_q[7]), .Qn(Interrupt_safe));  // open: preset, reset
  assign and_1_out = in_2[23:16] & {8{load_another}};  // AND_Gate and_1, 8 bits wide
  or or_1 (or_1_out, Interrupt_safe, load_another);
  or or_2 (PC_enable, load_another, Interrupt_safe);
  Counter #(.max('hf), .trigger("falling"), .width(4)) counter_1 (
    .load(load_check), .count(j_k_ff_1_q[7]), .clk(clock), .D(4'b0000), .Q(counter_1_q));  // open: clr, up, carry
  Register #(.trigger("falling")) register_1 (
    .D(in_2[23:16]), .en(Interrupt_safe), .clk(clock), .Q(register_1_q));  // open: clr
  assign and_2_out = register_1_q & {8{j_k_ff_1_q[7]}};  // AND_Gate and_2, 8 bits wide
  ROM #(.addrWidth(11)) rom_1 (.addr({and_2_out[6:0], counter_1_q}), .data(rom_1_data));
  RAM #(.addrWidth(11), .enables("line"), .\type ("nonvolatile")) ram_1 (
    .addr({and_2_out[6:0], counter_1_q}), .we(WCS_write), .clk(clock), .din(in_2[7:0]), .dout(ram_1_dout));
  Register #(.trigger("falling"), .width(24)) register_2 (
    .D({and_1_out, in_2[15:0]}), .en(or_1_out), .clk(clock), .Q(out_19));  // open: clr
  assign controlled_buffer_1_out = not_2_out ? rom_1_data : 8'bz;  // Controlled_Buffer controlled_buffer_1
  assign controlled_buffer_1_out = and_2_out[7] ? ram_1_dout : 8'bz;  // Controlled_Buffer controlled_buffer_2
  not not_2 (not_2_out, and_2_out[7]);
  Decoder #(.select(4)) decoder_1 (
    .out1(decoder_1_out1[0]), .out2(decoder_1_out1[1]), .out3(decoder_1_out1[2]), .out4(Page_write),
    .out5(load_another), .out6(A_write_indirect), .out7(B_write_indirect), .out8(PSW_compare), .out9(out_14),
    .out10(decoder_1_out1[9]), .out11(ALU_instruction), .out12(ALU_instruction_logical),
    .out13(Interrupt_enable), .out14(out_18), .out15(load_check), .sel(controlled_buffer_1_out[3:0]),
    .en(j_k_ff_1_q[7]));  // open: out0
  Register #(.trigger("high"), .width(1)) branch_true (
    .D(branch), .en(PSW_compare), .clk(clock), .Q(branch_true_q), .clr(Interrupt_safe));
  or or_3 (B_write, decoder_1_out1[2], B_write_indirect);
  or or_4 (or_4_out, ALU_instruction, ALU_instruction_logical);
  assign out_21 = or_4_out ? controlled_buffer_1_out[7:4] : 4'bz;  // Controlled_Buffer controlled_buffer_3
  or or_5 (a_write, decoder_1_out1[1], A_write_indirect);
  and and_3 (and_3_out, decoder_1_out1[9], branch_true_q);
  or or_6 (load, decoder_1_out1[0], out_14, and_3_out);

  // Notes on the sheet:
  //   contents of rom_1 (hex, n*v repeats v):
  //   16*f 1 15*f 6 5 fc 13*f 5 1 14*f 5 6 5 fc 12*f 2 15*f 3 15*f 7 15*f 6 15*f fc 15*f ac 15*f 8 5 a
  //   13*f 5 fc 14*f 5 2 14*f d 15*f 4 15*f 6 5 fc 5 6 11*f 7 5 ac 5 fc 11*f 9b 15*f fb 6 3c 13*f 5 fc
  //   14*f bc 15*f c 15*f ec 15*f 6c 15*f cb 111*f 5 2 14*f 5 3 14*f 8c 15*f 9c 15*f 9c 5 8 5 a 11*f 9
  //   15*f 7 5 ac 5 1 11*f 5 6 1422*f
endmodule

module PC (
  input  load,
  input  enable,
  input  clock,
  input  [23:0] data_in,
  input  interrupt,
  input  PC_writeback,
  input  Load_check,
  output [23:0] data_out
);

  wire and_1_out, and_2_out, j_k_ff_1_q, j_k_ff_2_q, not_1_out, not_2_out, s_r_ff_1_qn;
  wire [23:0] controlled_buffer_1_out, register_1_q;

  J_K_Flip_Flop j_k_ff_1 (.J(Load_check), .K(clock), .clk(clock), .Q(j_k_ff_1_q));  // open: Qn, preset, reset
  and and_1 (and_1_out, interrupt, clock);
  S_R_Flip_Flop s_r_ff_1 (.S(load), .R(j_k_ff_1_q), .clk(clock), .Qn(s_r_ff_1_qn));  // open: Q, reset, preset
  assign controlled_buffer_1_out = not_1_out ? data_in : 24'bz;  // Controlled_Buffer controlled_buffer_1
  not not_1 (not_1_out, PC_writeback);
  and and_2 (and_2_out, s_r_ff_1_qn, enable);
  assign controlled_buffer_1_out = PC_writeback ? register_1_q : 24'bz;  // Controlled_Buffer controlled_buffer_2
  Counter #(.max('hffffff), .width(24)) counter_1 (
    .clr(and_1_out), .load(load), .count(and_2_out), .clk(clock), .D(controlled_buffer_1_out), .Q(data_out));  // open: up, carry
  J_K_Flip_Flop j_k_ff_2 (.Q(j_k_ff_2_q), .preset(and_1_out), .reset(PC_writeback));  // open: J, K, clk, Qn
  not not_2 (not_2_out, j_k_ff_2_q);
  Register #(.width(24)) register_1 (.D(data_out), .en(not_2_out), .clk(clock), .Q(register_1_q));  // open: clr
endmodule

module ALU (
  input  C_out,
  input  A_write,
  input  B_write,
  input  clock,
  input  [23:0] in_5,
  input  [3:0] ALU_inst,
  input  ALU_logical,
  output [23:0] out_8,
  output carry_out,
  output EQ
);

  wire and_1_out, and_2_out, not_1_out, not_2_out, not_3_out, not_4_out;
  wire [23:0] alu_in_alu_1_c_out, register_1_q, register_2_q;

  Register #(.width(24)) register_1 (.D(in_5), .en(A_write), .clk(clock), .Q(register_1_q));  // open: clr
  Register #(.width(24)) register_2 (.D(in_5), .en(B_write), .clk(clock), .Q(register_2_q));  // open: clr
  not not_1 (not_1_out, ALU_inst[0]);
  not not_2 (not_2_out, ALU_inst[1]);
  not not_3 (not_3_out, ALU_inst[2]);
  and and_1 (and_1_out, not_1_out, not_2_out, not_3_out, ALU_inst[3], ALU_logical);
  not not_4 (not_4_out, and_1_out);
  ALU_IN_ALU alu_in_alu_1 (
    .A_in(register_1_q), .B_in(register_2_q), .Operand(ALU_inst), .carry_in(1'b0), .M_in(ALU_logical),
    .carry_out(carry_out), .C_out(alu_in_alu_1_c_out), .EQ(EQ));
  assign out_8 = and_1_out ? {register_1_q[0], register_1_q[23:1]} : 24'bz;  // Controlled_Buffer controlled_buffer_1
  and and_2 (and_2_out, C_out, not_4_out);
  assign out_8 = and_2_out ? alu_in_alu_1_c_out : 24'bz;  // Controlled_Buffer controlled_buffer_2
endmodule

module IO_subsystem (
  input  [23:0] data_in_IO,
  input  [23:0] Address_in_IO,
  input  Interupt_1,
  input  Interrupt_2,
  input  interrupt_3,
  input  interrrupt_4,
  input  interrupt_5,
  input  interrupt_safety,
  input  [5:0] interrput_vector,
  output [23:0] Data_out_IO,
  output [5:0] interupt_out,
  output [5:0] interrupt_handshake_return,
  output [19:0] Address_out_IO,
  output IO_data_access
);

  wire [2:0] priority_encoder_1_out;

  and and_1 (IO_data_access, Address_in_IO[20], Address_in_IO[21], Address_in_IO[22], Address_in_IO[23]);
  Priority_Encoder priority_encoder_1 (
    .in1(Interupt_1), .in2(Interrupt_2), .in3(interrupt_3), .in4(interrrupt_4), .in5(interrupt_5),
    .out(priority_encoder_1_out), .en_in(interrupt_safety));  // open: in0, in6, in7, gs, en_out
  Pull_Resistor pull_resistor_1 (.node(priority_encoder_1_out));
  Decoder #(.select(3)) decoder_1 (
    .out1(interrupt_handshake_return[0]), .out2(interrupt_handshake_return[1]),
    .out3(interrupt_handshake_return[2]), .out4(interrupt_handshake_return[3]),
    .out5(interrupt_handshake_return[4]), .out6(interrupt_handshake_return[5]), .sel(priority_encoder_1_out),
    .en(1'b1));  // open: out0, out7

  assign Address_out_IO = Address_in_IO[19:0];
  assign Data_out_IO = data_in_IO;
  assign interupt_out = interrput_vector;
endmodule

module PSW (
  input  [23:0] compare_word_in,
  input  clock,
  input  carry,
  input  equals,
  input  [5:0] interrupt_lines,
  input  ALU_inst,
  input  interrupt_enable_set,
  output Branch,
  output interrupt,
  output interrupt_enable
);

  wire and_1_out, and_3_out, and_4_out, and_5_out, and_6_out, and_7_out, and_8_out, and_9_out, and_10_out,
       or_1_out, register_1_q, register_2_q;
  wire [5:0] register_3_q;

  Register #(.trigger("falling"), .width(1)) register_1 (
    .D(carry), .en(ALU_inst), .clk(clock), .Q(register_1_q));  // open: clr
  Register #(.trigger("falling"), .width(1)) register_2 (
    .D(equals), .en(ALU_inst), .clk(clock), .Q(register_2_q));  // open: clr
  Register #(.trigger("high"), .width(6)) register_3 (
    .D(interrupt_lines), .en(interrupt), .clk(clock), .Q(register_3_q));  // open: clr
  S_R_Flip_Flop s_r_ff_1 (
    .Q(interrupt_enable), .reset(and_1_out), .preset(interrupt_enable_set));  // open: S, R, clk, Qn
  and and_1 (and_1_out, interrupt, clock);
  or or_1 (or_1_out, interrupt_lines[0], interrupt_lines[1], interrupt_lines[2], interrupt_lines[3], interrupt_lines[4], interrupt_lines[5]);
  and and_2 (interrupt, or_1_out, interrupt_enable);
  and and_3 (and_3_out, compare_word_in[0], register_1_q);
  and and_4 (and_4_out, compare_word_in[1], register_2_q);
  and and_5 (and_5_out, register_3_q[0], compare_word_in[2]);
  and and_6 (and_6_out, register_3_q[1], compare_word_in[3]);
  and and_7 (and_7_out, register_3_q[2], compare_word_in[4]);
  and and_8 (and_8_out, register_3_q[3], compare_word_in[5]);
  and and_9 (and_9_out, register_3_q[4], compare_word_in[6]);
  and and_10 (and_10_out, register_3_q[5], compare_word_in[7]);
  or or_2 (Branch, and_3_out, and_4_out, and_5_out, and_6_out, and_7_out, and_8_out, and_9_out, and_10_out);
endmodule

module TERMINAL (
  input  [23:0] IO_data,
  input  clock,
  input  [19:0] IO_address,
  input  IO_write,
  output [6:0] out_5,
  output clock_out
);

  wire and_1_out, and_2_out, and_3_out, and_4_out, and_5_out, not_2_out, not_3_out, not_4_out, register_1_q;
  wire [0:0] counter_1_q;
  wire [19:0] not_1_out;

  assign not_1_out = ~IO_address;  // NOT_Gate not_1, 20 bits wide
  Register #(.trigger("high"), .width(1)) register_1 (
    .D(1'b1), .en(and_4_out), .clk(1'b1), .Q(register_1_q), .clr(and_5_out));
  Counter #(.max('h3), .width(2)) counter_1 (
    .clr(and_5_out), .count(register_1_q), .clk(clock), .Q({clock_out, counter_1_q[0]}));  // open: load, up, D, carry
  not not_2 (not_2_out, register_1_q);
  and and_1 (and_1_out, not_2_out, and_4_out);
  not not_3 (not_3_out, not_1_out[1]);
  Register #(.trigger("high"), .width(7)) register_2 (
    .D(IO_data[6:0]), .en(and_1_out), .clk(1'b1), .Q(out_5));  // open: clr
  and and_2 (and_2_out, not_1_out[0], not_1_out[1], not_1_out[2], not_1_out[3], not_1_out[4], not_1_out[5], not_1_out[6], not_1_out[7], not_1_out[8], not_1_out[9], not_1_out[10], not_1_out[11], not_1_out[12], not_1_out[13], not_1_out[14], not_1_out[15], not_1_out[16], not_1_out[17], not_1_out[18], not_1_out[19], IO_write);
  and and_3 (and_3_out, not_1_out[0], not_3_out, not_1_out[2], not_1_out[3], not_1_out[4], not_1_out[5], not_1_out[6], not_1_out[7], not_1_out[8], not_1_out[9], not_1_out[10], not_1_out[11], not_1_out[12], not_1_out[13], not_1_out[14], not_1_out[15], not_1_out[16], not_1_out[17], not_1_out[18], not_1_out[19], IO_write);
  and and_4 (and_4_out, and_2_out, not_4_out);
  not not_4 (not_4_out, and_3_out);
  and and_5 (and_5_out, counter_1_q[0], clock_out);
endmodule

module ALU_IN_ALU (
  input  [23:0] A_in,
  input  [23:0] B_in,
  input  [3:0] Operand,
  input  carry_in,
  input  M_in,
  output carry_out,
  output [23:0] C_out,
  output EQ
);

  wire alu_condensed_1_cout, alu_condensed_1_eq, alu_condensed_2_cout, alu_condensed_2_eq,
       alu_condensed_3_cout, alu_condensed_3_eq, alu_condensed_4_cout, alu_condensed_4_eq,
       alu_condensed_5_cout, alu_condensed_5_eq, alu_condensed_6_cout, alu_condensed_6_eq, not_1_out;

  not not_1 (not_1_out, carry_in);
  ALU_condensed alu_condensed_1 (
    .A_in(A_in[3:0]), .B_in(B_in[3:0]), .instruction(Operand), .CIN(not_1_out), .M(M_in),
    .COUT(alu_condensed_1_cout), .EQ(alu_condensed_1_eq), .out_8(C_out[3:0]));
  ALU_condensed alu_condensed_2 (
    .A_in(A_in[7:4]), .B_in(B_in[7:4]), .instruction(Operand), .CIN(alu_condensed_1_cout), .M(M_in),
    .COUT(alu_condensed_2_cout), .EQ(alu_condensed_2_eq), .out_8(C_out[7:4]));
  ALU_condensed alu_condensed_3 (
    .A_in(A_in[11:8]), .B_in(B_in[11:8]), .instruction(Operand), .CIN(alu_condensed_2_cout), .M(M_in),
    .COUT(alu_condensed_3_cout), .EQ(alu_condensed_3_eq), .out_8(C_out[11:8]));
  and and_1 (EQ, alu_condensed_1_eq, alu_condensed_2_eq, alu_condensed_3_eq, alu_condensed_4_eq, alu_condensed_5_eq, alu_condensed_6_eq);
  ALU_condensed alu_condensed_4 (
    .A_in(A_in[15:12]), .B_in(B_in[15:12]), .instruction(Operand), .CIN(alu_condensed_3_cout), .M(M_in),
    .COUT(alu_condensed_4_cout), .EQ(alu_condensed_4_eq), .out_8(C_out[15:12]));
  ALU_condensed alu_condensed_5 (
    .A_in(A_in[19:16]), .B_in(B_in[19:16]), .instruction(Operand), .CIN(alu_condensed_4_cout), .M(M_in),
    .COUT(alu_condensed_5_cout), .EQ(alu_condensed_5_eq), .out_8(C_out[19:16]));
  ALU_condensed alu_condensed_6 (
    .A_in(A_in[23:20]), .B_in(B_in[23:20]), .instruction(Operand), .CIN(alu_condensed_5_cout), .M(M_in),
    .COUT(alu_condensed_6_cout), .EQ(alu_condensed_6_eq), .out_8(C_out[23:20]));
  not not_2 (carry_out, alu_condensed_6_cout);
endmodule

module ALU_condensed (
  input  [3:0] A_in,
  input  [3:0] B_in,
  input  [3:0] instruction,
  input  CIN,
  input  M,
  output COUT,
  output EQ,
  output [3:0] out_8
);

  wire and_1_out, and_2_out, and_3_out, and_4_out, and_5_out, and_6_out, and_7_out, and_8_out, and_9_out,
       and_10_out, and_11_out, and_12_out, and_13_out, and_14_out, and_15_out, and_16_out, and_17_out,
       and_18_out, and_19_out, and_20_out, and_21_out, and_22_out, and_23_out, and_24_out, and_25_out,
       and_26_out, and_27_out, and_28_out, and_29_out, and_30_out, and_31_out, and_32_out, buffer_1_out,
       nand_1_out, nand_3_out, nor_1_out, nor_2_out, nor_3_out, nor_4_out, nor_5_out, nor_6_out, nor_7_out,
       nor_8_out, nor_9_out, nor_10_out, nor_11_out, nor_12_out, not_1_out, not_2_out, not_3_out, not_4_out,
       not_5_out, not_6_out, not_7_out, not_8_out, not_9_out, not_10_out, not_11_out;

  not not_1 (not_1_out, B_in[3]);
  not not_2 (not_2_out, B_in[2]);
  not not_3 (not_3_out, B_in[1]);
  not not_4 (not_4_out, B_in[0]);
  not not_5 (not_5_out, M);
  and and_1 (and_1_out, B_in[3], instruction[3], A_in[3]);
  and and_2 (and_2_out, A_in[3], instruction[2], not_1_out);
  and and_3 (and_3_out, not_1_out, instruction[1]);
  and and_4 (and_4_out, instruction[0], B_in[3]);
  and and_5 (and_5_out, B_in[2], instruction[3], A_in[2]);
  and and_6 (and_6_out, A_in[2], instruction[2], not_2_out);
  and and_7 (and_7_out, not_2_out, instruction[1]);
  and and_8 (and_8_out, instruction[0], B_in[2]);
  and and_9 (and_9_out, B_in[1], instruction[3], A_in[1]);
  and and_10 (and_10_out, A_in[1], instruction[2], not_3_out);
  and and_11 (and_11_out, not_3_out, instruction[1]);
  and and_12 (and_12_out, instruction[0], B_in[1]);
  and and_13 (and_13_out, B_in[0], instruction[3], A_in[0]);
  and and_14 (and_14_out, A_in[0], instruction[2], not_4_out);
  and and_15 (and_15_out, not_4_out, instruction[1]);
  and and_16 (and_16_out, instruction[0], B_in[0]);
  nor nor_1 (nor_1_out, and_1_out, and_2_out);
  nor nor_2 (nor_2_out, and_3_out, and_4_out, A_in[3]);
  nor nor_3 (nor_3_out, and_5_out, and_6_out);
  nor nor_4 (nor_4_out, and_7_out, and_8_out, A_in[2]);
  nor nor_5 (nor_5_out, and_9_out, and_10_out);
  nor nor_6 (nor_6_out, and_11_out, and_12_out, A_in[1]);
  nor nor_7 (nor_7_out, and_13_out, and_14_out);
  nor nor_8 (nor_8_out, and_15_out, and_16_out, A_in[0]);
  not not_6 (not_6_out, nor_8_out);
  buf buffer_1 (buffer_1_out, nor_2_out);
  and and_17 (and_17_out, nor_1_out, nor_4_out);
  and and_18 (and_18_out, nor_1_out, nor_3_out, nor_6_out);
  and and_19 (and_19_out, nor_1_out, nor_3_out, nor_5_out, nor_8_out);
  nand nand_1 (nand_1_out, nor_1_out, nor_3_out, nor_5_out, nor_7_out, CIN);
  // NAND_Gate nand_2 has open pins: in0=nor_1_out, in1=nor_3_out, in2=nor_5_out, in3=nor_7_out, out=open
  not not_7 (not_7_out, nor_2_out);
  and and_20 (and_20_out, CIN, nor_7_out, nor_5_out, nor_3_out, not_5_out);
  and and_21 (and_21_out, nor_5_out, nor_3_out, nor_8_out, not_5_out);
  and and_22 (and_22_out, nor_3_out, nor_6_out, not_5_out);
  and and_23 (and_23_out, nor_4_out, not_5_out);
  not not_8 (not_8_out, nor_4_out);
  and and_24 (and_24_out, CIN, nor_7_out, nor_5_out, not_5_out);
  and and_25 (and_25_out, nor_5_out, nor_8_out, not_5_out);
  and and_26 (and_26_out, nor_6_out, not_5_out);
  not not_9 (not_9_out, nor_6_out);
  and and_27 (and_27_out, CIN, nor_7_out, not_5_out);
  and and_28 (and_28_out, nor_8_out, not_5_out);
  and and_29 (and_29_out, nor_7_out, not_6_out);
  nand nand_3 (nand_3_out, CIN, not_5_out);
  nor nor_9 (nor_9_out, buffer_1_out, and_17_out, and_18_out, and_19_out);
  and and_30 (and_30_out, nor_1_out, not_7_out);
  nor nor_10 (nor_10_out, and_20_out, and_21_out, and_22_out, and_23_out);
  and and_31 (and_31_out, nor_3_out, not_8_out);
  nor nor_11 (nor_11_out, and_24_out, and_25_out, and_26_out);
  and and_32 (and_32_out, nor_5_out, not_9_out);
  nor nor_12 (nor_12_out, and_27_out, and_28_out);
  not not_10 (not_10_out, nor_9_out);
  not not_11 (not_11_out, nand_1_out);
  xor xor_1 (out_8[3], and_30_out, nor_10_out);
  xor xor_2 (out_8[2], and_31_out, nor_11_out);
  xor xor_3 (out_8[1], and_32_out, nor_12_out);
  xor xor_4 (out_8[0], and_29_out, nand_3_out);
  or or_1 (COUT, not_10_out, not_11_out);
  and and_33 (EQ, out_8[2], out_8[3], out_8[0], out_8[1]);
endmodule

module page_handler (
  input  [23:0] in_1,
  input  [3:0] Page_in,
  input  page_write,
  input  clock,
  output [23:0] out_5
);

  wire [3:0] register_1_q;

  Register #(.width(4)) register_1 (.D(Page_in), .en(page_write), .clk(clock), .Q(register_1_q));  // open: clr
  or or_1 (out_5[18], in_1[18], register_1_q[1]);
  or or_2 (out_5[19], in_1[19], register_1_q[2]);
  or or_3 (out_5[20], in_1[20], register_1_q[3]);
  or or_4 (out_5[17], in_1[17], register_1_q[0]);

  assign {out_5[23:21], out_5[16:0]} = {in_1[23:21], in_1[16:0]};
endmodule

module keybd (
  input  in_1,
  input  [7:0] in_2,
  input  clock,
  input  [5:0] interrupt_handshake,
  input  [19:0] address_In,
  input  IO_write,
  output [23:0] data_out,
  output interrupt,
  output [5:0] out_9,
  output out_10
);

  wire and_1_out, and_2_out, and_3_out, and_4_out, and_5_out, and_6_out, and_7_out, counter_1_carry,
       counter_1_q, not_1_out, not_2_out, not_3_out, not_4_out, not_5_out, not_6_out, not_7_out, not_8_out,
       not_9_out, not_10_out, not_11_out, not_12_out, not_13_out, not_14_out, not_15_out, not_16_out,
       not_17_out, not_18_out, not_19_out, not_20_out, not_21_out, not_22_out, not_23_out, s_r_ff_1_q,
       s_r_ff_2_q, s_r_ff_3_q, s_r_ff_4_q, s_r_ff_4_qn, s_r_ff_5_qn;
  wire [7:0] register_1_q, register_2_q;

  not not_1 (not_1_out, address_In[0]);
  not not_2 (not_2_out, address_In[2]);
  not not_3 (not_3_out, address_In[3]);
  not not_4 (not_4_out, address_In[4]);
  not not_5 (not_5_out, address_In[5]);
  not not_6 (not_6_out, address_In[6]);
  not not_7 (not_7_out, address_In[7]);
  not not_8 (not_8_out, address_In[8]);
  not not_9 (not_9_out, address_In[9]);
  not not_10 (not_10_out, address_In[10]);
  not not_11 (not_11_out, address_In[11]);
  not not_12 (not_12_out, address_In[12]);
  not not_13 (not_13_out, address_In[13]);
  not not_14 (not_14_out, address_In[14]);
  not not_15 (not_15_out, address_In[15]);
  not not_16 (not_16_out, address_In[16]);
  not not_17 (not_17_out, address_In[17]);
  not not_18 (not_18_out, address_In[18]);
  not not_19 (not_19_out, address_In[19]);
  Register #(.trigger("high")) register_1 (.D(in_2), .en(1'b1), .clk(1'b1), .Q(register_1_q));  // open: clr
  and and_1 (and_1_out, not_1_out, address_In[1], not_2_out, not_3_out, not_4_out, not_5_out, not_6_out, not_7_out, not_8_out, not_9_out, not_10_out, not_11_out, not_12_out, not_13_out, not_14_out, not_15_out, not_16_out, not_17_out, not_18_out, not_19_out, IO_write);
  S_R_Flip_Flop s_r_ff_1 (.Q(s_r_ff_1_q), .reset(counter_1_carry), .preset(and_2_out));  // open: S, R, clk, Qn
  and and_2 (and_2_out, clock, in_1);
  Counter #(.max('h1), .width(1)) counter_1 (
    .clr(counter_1_carry), .count(s_r_ff_1_q), .clk(clock), .carry(counter_1_carry), .Q(counter_1_q));  // open: load, up, D
  Register register_2 (.D(register_1_q), .en(in_1), .clk(clock), .Q(register_2_q));  // open: clr
  not not_20 (not_20_out, interrupt_handshake[3]);
  S_R_Flip_Flop #(.trigger("falling")) s_r_ff_2 (
    .Q(s_r_ff_2_q), .reset(s_r_ff_4_qn), .preset(interrupt_handshake[3]));  // open: S, R, clk, Qn
  assign out_9 = interrupt_handshake[3] ? 6'b001000 : 6'bz;  // Controlled_Buffer controlled_buffer_1
  and and_3 (and_3_out, not_20_out, s_r_ff_2_q);
  assign data_out = and_1_out ? {{16{1'b0}}, register_2_q} : 24'bz;  // Controlled_Buffer controlled_buffer_2
  not not_21 (not_21_out, interrupt_handshake[3]);
  S_R_Flip_Flop #(.trigger("falling")) s_r_ff_3 (
    .Q(s_r_ff_3_q), .reset(s_r_ff_5_qn), .preset(interrupt_handshake[3]));  // open: S, R, clk, Qn
  S_R_Flip_Flop #(.trigger("high")) s_r_ff_4 (
    .Q(s_r_ff_4_q), .reset(and_4_out), .Qn(s_r_ff_4_qn), .preset(counter_1_q));  // open: S, R, clk
  buf and_4 (and_4_out, and_3_out);  // AND_Gate
  and and_5 (and_5_out, not_21_out, s_r_ff_3_q);
  not not_22 (not_22_out, interrupt);
  and and_6 (and_6_out, not_22_out, not_23_out, s_r_ff_4_q);
  S_R_Flip_Flop #(.trigger("high")) s_r_ff_5 (
    .Q(interrupt), .reset(and_7_out), .Qn(s_r_ff_5_qn), .preset(and_6_out));  // open: S, R, clk
  not not_23 (not_23_out, and_7_out);
  and and_7 (and_7_out, clock, and_5_out);

  assign out_10 = in_1;
endmodule

module timer (
  input  [5:0] interrupt_handshake,
  input  clock,
  output interrupt,
  output [5:0] out_4
);

  wire and_1_out, and_2_out, and_3_out, not_1_out, s_r_ff_1_q, s_r_ff_2_qn;
  wire [17:0] counter_1_q;

  Counter #(.max('h3ffff), .width(18)) counter_1 (
    .clr(and_1_out), .clk(clock), .Q(counter_1_q));  // open: load, up, count, D, carry
  and and_1 (and_1_out, counter_1_q[17], counter_1_q[0]);
  assign out_4 = interrupt_handshake[2] ? 6'b000100 : 6'bz;  // Controlled_Buffer controlled_buffer_1
  not not_1 (not_1_out, interrupt_handshake[2]);
  S_R_Flip_Flop #(.trigger("falling")) s_r_ff_1 (
    .Q(s_r_ff_1_q), .reset(s_r_ff_2_qn), .preset(interrupt_handshake[2]));  // open: S, R, clk, Qn
  and and_2 (and_2_out, not_1_out, s_r_ff_1_q);
  S_R_Flip_Flop s_r_ff_2 (
    .Q(interrupt), .reset(and_3_out), .Qn(s_r_ff_2_qn), .preset(counter_1_q[17]));  // open: S, R, clk
  and and_3 (and_3_out, clock, and_2_out);
endmodule

module software_interrupt (
  input  [5:0] handshake,
  input  clock,
  input  st_interrupt,
  output interrupt,
  output [5:0] interrupt_vector
);

  wire and_1_out, and_2_out, not_1_out, s_r_ff_1_q, s_r_ff_2_qn;

  assign interrupt_vector = handshake[0] ? 6'b000010 : 6'bz;  // Controlled_Buffer controlled_buffer_1
  not not_1 (not_1_out, handshake[0]);
  S_R_Flip_Flop #(.trigger("falling")) s_r_ff_1 (
    .Q(s_r_ff_1_q), .reset(s_r_ff_2_qn), .preset(handshake[0]));  // open: S, R, clk, Qn
  and and_1 (and_1_out, not_1_out, s_r_ff_1_q);
  S_R_Flip_Flop s_r_ff_2 (
    .Q(interrupt), .reset(and_2_out), .Qn(s_r_ff_2_qn), .preset(st_interrupt));  // open: S, R, clk
  and and_2 (and_2_out, clock, and_1_out);
endmodule
